# Fritzing sketch Nano_Hall_TM1637 (saved by Fritzing 0.9.9b)
breadboards: 1

parts:
  Part1 = TM1637
  Mod1 = KY-035 Analog Magnetic Hall Sensor [package="Breakout board"]
  Part2 = Arduino Nano (Rev3.0)

nets:
  GND: Part1.GND, Mod1.Vin
  N1: Part1.VCC, Mod1.-
  N2: Part1.DIO, Part2.D7
  N3: Part1.CLK, Part2.D6
  N4: Mod1.S, Part2.A0

custom parts:
  TM1637: A 4 7-seg display
  KY-035 Analog Magnetic Hall Sensor: KY-035 analog magnetic hall sensor is a module that reacts in the presence of a magnet. It can measure the polarity and relative strength of a magnetic field.
